# Fritzing sketch ASMEDesignCompetition (saved by Fritzing 0.7.12b)
breadboards: 2

parts:
  ArduinoUnoR3SMD = Arduino
  VIN = Battery block 9V
  PWM_LEFT = female pin header, 2 pins [form="♀ (female)"]
  LEFT_IN1 = female pin header, 2 pins [form="♀ (female)"]
  LEFT_IN2 = female pin header, 2 pins [form="♀ (female)"]
  STBY = female pin header, 2 pins [form="♀ (female)"]
  PWM_RIGHT = female pin header, 2 pins [form="♀ (female)"]
  RIGHT_IN1 = female pin header, 2 pins [form="♀ (female)"]
  RIGHT_IN2 = female pin header, 2 pins [form="♀ (female)"]
  VCC = female pin header, 2 pins [form="♀ (female)"]
  LeftMotorReg = Voltage Regulator - 5V [package="TO220 [THT]"]
  RightMotorReg = Voltage Regulator - 5V [package="TO220 [THT]"]
  R_MotorPow = female pin header, 2 pins [form="♀ (female)"]
  L_MotorPow = female pin header, 2 pins [form="♀ (female)"]
  ServoReg2 = Voltage Regulator - 5V [package="TO220 [THT]"]
  ServoReg1 = Voltage Regulator - 5V [package="TO220 [THT]"]
  ClawUp = Basic Servo
  CamTilt = Basic Servo
  ClawOpen = Basic Servo
  CamPan = Basic Servo
  Cer_OPEN = Ceramic Capacitor [capacitance=0.1µF package="100 mil [THT, multilayer]"]
  Cer_PAN = Ceramic Capacitor [capacitance=0.1µF package="100 mil [THT, multilayer]"]
  Cer_UP = Ceramic Capacitor [capacitance=0.1µF package="100 mil [THT, multilayer]"]
  Cer_TILT = Ceramic Capacitor [capacitance=0.1µF package="100 mil [THT, multilayer]"]
  C_SerReg2 = Electrolytic Capacitor [capacitance=1mF package="100 mil [THT, electrolytic]"]
  C_SerReg1 = Electrolytic Capacitor [capacitance=1mF package="100 mil [THT, electrolytic]"]
  C_UP = Electrolytic Capacitor [capacitance=1mF package="100 mil [THT, electrolytic]"]
  C_TILT = Electrolytic Capacitor [capacitance=1mF package="100 mil [THT, electrolytic]"]
  C_PAN = Electrolytic Capacitor [capacitance=1mF package="100 mil [THT, electrolytic]"]
  C_OPEN = Electrolytic Capacitor [capacitance=1mF package="100 mil [THT, electrolytic]"]
  C_RMotReg = Electrolytic Capacitor [capacitance=0.1mF package="100 mil [THT, electrolytic]"]
  C_LMotReg = Electrolytic Capacitor [capacitance=0.1mF package="100 mil [THT, electrolytic]"]
  Cer_LMotReg = Ceramic Capacitor [capacitance=0.1µF package="100 mil [THT, multilayer]"]
  Cer_RMotReg = Ceramic Capacitor [capacitance=0.1µF package="100 mil [THT, multilayer]"]
  C_VinMot = Electrolytic Capacitor [capacitance=1mF package="100 mil [THT, electrolytic]"]
  C_VinServ = Electrolytic Capacitor [capacitance=1mF package="100 mil [THT, electrolytic]"]

nets:
  N1: ArduinoUnoR3SMD.D13, RIGHT_IN1.pin1, RIGHT_IN1.pin2
  N2: ArduinoUnoR3SMD.D12, RIGHT_IN2.pin1, RIGHT_IN2.pin2
  N3: ArduinoUnoR3SMD.D11, CamTilt.pulse
  N4: ArduinoUnoR3SMD.D10, CamPan.pulse
  N5: ArduinoUnoR3SMD.D9, ClawUp.pulse
  N6: ArduinoUnoR3SMD.D8, LEFT_IN2.pin1, LEFT_IN2.pin2
  N7: ArduinoUnoR3SMD.D7, LEFT_IN1.pin1, LEFT_IN1.pin2
  N8: ArduinoUnoR3SMD.D6, ClawOpen.pulse
  N9: ArduinoUnoR3SMD.D5, PWM_RIGHT.pin1, PWM_RIGHT.pin2
  N10: ArduinoUnoR3SMD.D4, STBY.pin1, STBY.pin2
  N11: ArduinoUnoR3SMD.D3, PWM_LEFT.pin1, PWM_LEFT.pin2
  N12: ArduinoUnoR3SMD.3V3, VCC.pin1, VCC.pin2
  GND: ArduinoUnoR3SMD.GND, VIN.-, LeftMotorReg.GND, RightMotorReg.GND, R_MotorPow.pin2, L_MotorPow.pin2, ServoReg2.GND, ServoReg1.GND, ClawUp.gnd, CamTilt.gnd, ClawOpen.gnd, CamPan.gnd, Cer_OPEN.1, Cer_PAN.1, Cer_UP.1, Cer_TILT.1, C_SerReg2.-, C_SerReg1.-, C_UP.-, C_TILT.-, C_PAN.-, C_OPEN.-, C_RMotReg.+, C_LMotReg.-, Cer_LMotReg.1, Cer_RMotReg.0, C_VinMot.-, C_VinServ.-
  N13: ArduinoUnoR3SMD.VIN, VIN.+, LeftMotorReg.input_voltage, RightMotorReg.input_voltage, ServoReg2.input_voltage, ServoReg1.input_voltage, C_VinMot.+, C_VinServ.+
  N14: LeftMotorReg.output_voltage, L_MotorPow.pin1, C_LMotReg.+, Cer_LMotReg.0
  N15: RightMotorReg.output_voltage, R_MotorPow.pin1, C_RMotReg.-, Cer_RMotReg.1
  VCC: ServoReg2.output_voltage, ClawOpen.vcc, CamPan.vcc, Cer_OPEN.0, Cer_PAN.0, C_SerReg2.+, C_PAN.+, C_OPEN.+
  VCC_2: ServoReg1.output_voltage, ClawUp.vcc, CamTilt.vcc, Cer_UP.0, Cer_TILT.0, C_SerReg1.+, C_UP.+, C_TILT.+
